# Fritzing sketch temperatura2-buttons (saved by Fritzing 0.9.1b)
circuit board: 7cm x 2cm
breadboards: 1

parts:
  S1 = Pushbutton [package="[THT]"]
  S2 = Pushbutton [package="[THT]"]
  S3 = Pushbutton [package="[THT]"]
  S4 = Pushbutton [package="[THT]"]
  J1 = male pin header, 3 pins [form="♂ (male)"]
  R2 = Resistor [tolerance=±5% resistance=330 package=THT]
  R3 = Resistor [tolerance=±5% resistance=620 package=THT]
  R4 = Resistor [tolerance=±5% resistance=1k package=THT]
  R5 = Resistor [tolerance=±5% resistance=3.3k package=THT]
  R1 = Resistor [tolerance=±5% resistance=2.2k package=THT]
  S5 = Pushbutton [package="[THT]"]

nets (from the schematic view):
  GND: S1.Pin_1, S1.Pin_2, S2.Pin_1, S2.Pin_2, S3.Pin_1, S3.Pin_2, S4.Pin_1, S4.Pin_2, J1.pin2, S5.Pin_1, S5.Pin_2
  N1: S1.Pin_3, S1.Pin_4, J1.pin3, R2.Pin_0, R1.Pin_1
  N2: S2.Pin_3, S2.Pin_4, R2.Pin_1, R3.Pin_0
  N3: S3.Pin_3, S3.Pin_4, R3.Pin_1, R4.Pin_0
  N4: S4.Pin_3, S4.Pin_4, R4.Pin_1, R5.Pin_0
  N5: J1.pin1, R1.Pin_0
  N6: R5.Pin_1, S5.Pin_3, S5.Pin_4
