# Fritzing sketch temperatura2-display (saved by Fritzing 0.8.7b)
circuit board: 5cm x 2cm
breadboards: 1

parts:
  U1 = LCD-16X2 [package=lcd-16x2]
  R1 = Resistor [tolerance=±5% resistance=2.2k package=THT]
  R2 = Resistor [tolerance=±5% resistance=2.2k package=THT]
  J1 = male pin header, 8 pins [form="♂ (male)"]

nets:
  N1: U1.VSS, U1.R_W, U1.K, R1.Pin_1, J1.pin8
  N2: U1.VDD, R2.Pin_1, J1.pin1
  N3: U1.VO, R1.Pin_0
  N4: U1.RS, J1.pin2
  N5: U1.E, J1.pin3
  N6: U1.DB4, J1.pin4
  N7: U1.DB5, J1.pin5
  N8: U1.DB6, J1.pin6
  N9: U1.DB7, J1.pin7
  N10: U1.A, R2.Pin_0
