# Fritzing sketch temperatura2 (saved by Fritzing 0.9.1b)
circuit board: 10cm x 9cm
breadboards: 3

parts:
  U2 = atmega328 [package=dip]
  S1 = Pushbutton [package="[THT]"]
  XTAL1 = Crystal [frequency="16 Mhz" package=THT]
  C5 = Ceramic Capacitor [capacitance=27pF voltage=50V package="200 mil [THT, multilayer]"]
  R2 = Resistor [tolerance=±5% resistance=1k package=THT]
  C1 = Electrolytic Capacitor [capacitance=47µF voltage=35V package="100 mil [THT, electrolytic]"]
  U1 = Voltage Regulator - 5V [package="TO220 [THT]"]
  C3 = Electrolytic Capacitor [capacitance=47µF voltage=16V package="100 mil [THT, electrolytic]"]
  LED1 = LED - 5mm [color="Red (633nm)" package="5 mm [THT]"]
  R1 = Resistor [tolerance=±5% resistance=330 package=THT]
  J1 = Power Jack [package=power_jack_pth]
  D1 = Rectifier Diode [part_number=1N4007 package="300 mil [THT]"]
  R3 = Resistor [tolerance=±5% resistance=330 package=THT]
  LED2 = LED - 5mm [color="Yellow (595nm)" package="5 mm [THT]"]
  R4 = Resistor [tolerance=±5% resistance=4.7k package=THT]
  C2 = Ceramic Capacitor [capacitance=100nF voltage=35V package="100 mil [THT, multilayer]"]
  C4 = Ceramic Capacitor [capacitance=100nF package="100 mil [THT, multilayer]"]
  J3 = male pin header, 3 pins [form="♂ (male)"]
  J2 = male pin header, 3 pins [form="♂ (male)"]
  U3 = TLP621 [package=THT]
  R7 = Resistor [tolerance=±5% resistance=1k package=THT]
  LED3 = LED - 5mm [color="Green (555nm)" package="5 mm [THT]"]
  J6 = screw terminal, 3 pins
  Q1 = NPN-Transistor [package="TO92 [THT]"]
  R8 = Resistor [tolerance=±5% resistance=620 package=THT]
  D2 = Rectifier Diode [part_number=1N4007 package="300 mil [THT]"]
  K2 = Relay T73
  D3 = Rectifier Diode [part_number=1N4007 package="300 mil [THT]"]
  J8 = screw terminal, 3 pins
  Q2 = NPN-Transistor [package="TO92 [THT]"]
  U4 = TLP621 [package=THT]
  R9 = Resistor [tolerance=±5% resistance=1k package=THT]
  LED4 = LED - 5mm [color="Green (555nm)" package="5 mm [THT]"]
  R10 = Resistor [tolerance=±5% resistance=620 package=THT]
  J4 = male pin header, 16 pins [form="♂ (male)"]
  R5 = Resistor [tolerance=±5% resistance=2.2k package=THT]
  C6 = Ceramic Capacitor [capacitance=27pF voltage=50V package="200 mil [THT, multilayer]"]
  J5 = male pin header, 3 pins [form="♂ (male)"]
  J7 = male pin header, 3 pins [form="♂ (male)"]
  R6 = Resistor [tolerance=±5% resistance=2.2k package=THT]
  K1 = Relay T73

nets:
  N1: U2.RESET, S1.Pin_1, S1.Pin_2, R2.Pin_0
  N2: U2.D3_(PWM), J4.pin6
  N3: U2.D4, J4.pin4
  N4: U2.VCC, U2.AVCC, R2.Pin_1, U1.output_voltage, C3.+, R1.Pin_1, R4.Pin_0, C4.1, J3.pin3, J2.pin1, J4.pin2, R5.Pin_1, R6.Pin_1
  GND: U2.GND, S1.Pin_3, S1.Pin_4, C5.1, C1.-, U1.GND, C3.-, LED1.cathode, J1.GND, J1.GNDBREAK, LED2.cathode, C2.1, C4.0, J3.pin1, J2.pin2, LED3.anode, Q1.C, Q2.C, LED4.anode, J4.pin1, J4.pin5, J4.pin7, J4.pin8, J4.pin9, J4.pin10, J4.pin16, C6.1, J5.pin3, J7.pin3
  N5: U2.XLAT1, XTAL1.pin_1, C5.0
  N6: U2.XLAT2, XTAL1.pin_0, C6.0
  N7: U2.D5_(PWM), J4.pin11
  N8: U2.D6_(PWM), J4.pin12
  N9: U2.D7, J4.pin13
  N10: U2.D8, J4.pin14
  N11: U2.D9_(PWM), R4.Pin_1, J3.pin2
  N12: U2.D11_(PWM), R9.Pin_0
  N13: U2.D12, R7.Pin_0
  N14: U2.D13, R3.Pin_1
  N15: U2.A0, J2.pin3
  N16: C1.+, U1.input_voltage, D1.cathode, C2.0, U3.Pin_4, D2.cathode, K2.C2, D3.cathode, U4.Pin_4, J5.pin1, J7.pin1, K1.C2
  N17: LED1.anode, R1.Pin_0
  N18: J1.PWR, D1.anode
  N19: R3.Pin_0, LED2.anode
  N20: U3.Pin_1, R7.Pin_1
  N21: U3.Pin_2, LED3.cathode
  N22: U3.Pin_3, R8.Pin_0, J5.pin2
  N23: J6.pin1, K1.NC
  N24: J6.pin2, K1.COM
  N25: J6.pin3, K1.NO
  N26: Q1.E, D2.anode, K1.C1
  N27: Q1.B, R8.Pin_1
  N28: K2.C1, D3.anode, Q2.E
  N29: K2.COM, J8.pin2
  N30: K2.NO, J8.pin3
  N31: K2.NC, J8.pin1
  N32: Q2.B, R10.Pin_1
  N33: U4.Pin_1, R9.Pin_1
  N34: U4.Pin_2, LED4.cathode
  N35: U4.Pin_3, R10.Pin_0, J7.pin2
  N36: J4.pin3, R5.Pin_0
  N37: J4.pin15, R6.Pin_0

custom parts:
  Relay T73: An T73 Mini PCB Relay

// code stored in the sketch: temp_maturador.ino
/* 
 Temperatura  
 Is a temperature controller with two relay to control Heating and Cooling.Those relay are photocoupler;
 
 The thermostat use 3 wire, two to power and one to signal. This use port digital 9;
 The relay A use port digital 11.
 The relay B use port digital 12;
 The keyboard controls the raising and lowering of the temperature, and use port analog 0 
 */
#include <OneWire.h>
#include <LiquidCrystal.h>
#include <EEPROM.h>

//Variaveis reles
int releA = 11;
int releB = 12;
long delayB = 10000;
float tempA = 18;
float tempB = 19;
float tempDelay = 0.5;
int statusA = LOW;
int statusB = LOW;
//Variaveis temperatura
int termometro = 9;
float temp;
//Variaveis keyboard
int keyboard = 0;
long valorKey = 0;
boolean alterouTemp = false;
//Variais serial
String inputString = "";         // a string to hold incoming data
boolean stringComplete = false;  // whether the string is complete
//Variaveis diversas
int led = 13;
long delayStart = 2000;
//Inicializacao bibliotecas
OneWire ds(termometro); 
LiquidCrystal lcd(4, 3, 5, 6, 7, 8);

void setup(void) {
  lcd.begin(16, 2);
  lcd.print("Temperatura!");
  lcd.setCursor(0,1);
  lcd.print(" Aguarde... ");      

  pinMode(releA, OUTPUT);
  pinMode(releB, OUTPUT);
  pinMode(A0, INPUT);
  pinMode(termometro, INPUT);
  pinMode(led, OUTPUT);     

  Serial.begin(9600);
  inputString.reserve(200);

  //Debug fixa valor de A e B
  //writeFloat(2, (10));
  //writeFloat(6, (11));
  //releA
  tempA = (float) (readFloat(2)-10);
  //releB
  tempB = (float) (readFloat(6)-10);
}

void loop(void) {
  digitalWrite(led, HIGH);  

  if (delayStart <= 0) {
    //Le botoes
    valorKey = analogRead(keyboard);
    if (stringComplete) {
      Serial.print(inputString);
      valorKey = inputString.toInt();
      // clear the string:
      inputString = "";
      stringComplete = false;
    }
    
    // lcd.clear();
    lcd.setCursor(12,0); 
    lcd.print("    ");
    lcd.setCursor(12,0); 
    lcd.print(valorKey,1);

    if(valorKey > 700 && valorKey < 800){
      tempA = tempA - 0.5;
      alterouTemp=true;
    }
    else if(valorKey > 400 && valorKey < 500){
      tempA = tempA + 0.5;    
      alterouTemp=true;
    }
    else if(valorKey > 300 && valorKey < 400){
      tempB = tempB - 0.5;      
      alterouTemp = true;
    }
    else if(valorKey > 100 && valorKey < 200){
      tempB = tempB + 0.5;    
      alterouTemp = true;
    }
    
    //Processa temperatura
    temp = getTemp();

    float tempXA = tempA;
    if (statusA == HIGH){
      tempXA += tempDelay;
    }    
    float tempXB = tempB;
    if (statusB == HIGH){
      tempXB -= tempDelay;
    }  
    if (temp <= tempXA){
      statusA = HIGH;
    } 
    else {
      statusA = LOW;
    }  
    if (temp >= tempXB){    
      if (delayB <= 0) {
        statusB = HIGH;
      }
    } 
    else {
      if (statusB == HIGH) {
        delayB = 240000;
      }
      statusB = LOW;    
    }    
    digitalWrite(releA, statusA);
    digitalWrite(releB, statusB);  

    //Imprime na serial
    /*Serial.print(tempXA);
     Serial.print(' ');
     Serial.print(statusA);
     Serial.print(' ');
     Serial.print(tempXB);
     Serial.print(' ');
     Serial.print(statusB);
     Serial.print(' ');
     Serial.print(temp);
     Serial.print(' ');
     Serial.println(delayB);*/

    //Imprime no display
    //lcd.noDisplay();
    //lcd.clear();
    lcd.setCursor(0,0);
    lcd.print("Temp:");
    lcd.setCursor(6,0);
    lcd.print(temp,1);
    lcd.setCursor(0,1);
    lcd.print(statusA,1);
    lcd.print(statusB,1);
    lcd.print(" ");
    lcd.print(tempXA,1);
    lcd.print(" ");
    lcd.print(tempXB,1);
    lcd.print(" ");
    lcd.print((delayB/1000),1);
    //lcd.display();

    //Controle de delay para motor da geladeira
    if (delayB > 0) {
      delayB -= 250;
    }  

    //Grava temperatura na memoria
    if (alterouTemp){
      //releA
      writeFloat(2, (tempA+10));
      //releB
      writeFloat(6, (tempB+10));
      alterouTemp = false;
    }
  } 
  else {
    delayStart -= 250;
    if (delayStart <= 0){
      analogRead(keyboard);
      getTemp();
      lcd.clear();
    }
  }

  digitalWrite(led, LOW);
  delay(250);   
}

//Funcoes do sistema
float getTemp(){
  byte data[12];
  byte addr[8];

  if ( !ds.search(addr)) {
    //no more sensors on chain, reset search
    ds.reset_search();
    return -1000;
  }

  if ( OneWire::crc8( addr, 7) != addr[7]) {
    //Serial.println("CRC is not valid!");
    return -1000;
  }

  if ( addr[0] != 0x10 && addr[0] != 0x28) {
    //Serial.print("Device is not recognized");
    return -1000;
  }

  ds.reset();
  ds.select(addr);
  ds.write(0x44,1); 

  byte present = ds.reset();
  ds.select(addr);
  ds.write(0xBE); 

  for (int i = 0; i < 9; i++) { 
    data[i] = ds.read();
  }

  ds.reset_search();

  byte MSB = data[1];
  byte LSB = data[0];

  float TRead = ((MSB << 8) | LSB); 
  float Temperature = TRead / 16;

  return Temperature;
}

void serialEvent() {
  while (Serial.available()) {
    char inChar = (char)Serial.read();
    inputString += inChar;    
    if (inChar == '\n'  || inChar == '\r\n'){
      stringComplete = true;
    }
  }
}

float readFloat(unsigned int addr) {
  union{
    byte b[4];
    float f;
  } 
  data;
  for(int i = 0; i < 4; i++){
    data.b[i] = EEPROM.read(addr+i);
  }
  return data.f;
}

void writeFloat(unsigned int addr, float x){
  union {
    byte b[4];
    float f;
  } 
  data;
  data.f = x;
  for(int i = 0; i < 4; i++) {
    EEPROM.write(addr+i, data.b[i]);
  }
}
